// Logisim project My CPU Part 13.circ as structural Verilog: 4 circuits, main circuit main
module main (
  output [7:0] out_1
);

  wire and_1_out, clock_1_out, not_1_out;
  wire [3:0] alu_1_alu_state_out, alu_state_out_decoder_1_state_out, counter_1_q, internal_screen_1__1_digit,
       internal_screen_1__2_digit;
  wire [7:0] A_Register_q, B_Register_q, controlled_buffer_1_out, counter_2_q, Jump_Register_q, register_2_q,
       register_3_q, X_Register_q, Y_Register_q;
  wire [15:0] register_1_q;
  wire [31:0] rom_1_data;

  Register #(.width(16), .trigger("low")) register_1 (
    .D({alu_state_out_decoder_1_state_out, register_2_q, counter_1_q}), .en(1'b1), .Q(register_1_q),
    .clk(clock_1_out));  // open: clr
  Register #(.trigger("falling")) register_2 (
    .D(out_1), .en(1'b1), .Q(register_2_q), .clk(rom_1_data[24]));  // open: clr
  Clock clock_1 (.out(clock_1_out));
  ROM #(.addrWidth(16), .dataWidth(32)) rom_1 (.addr(register_1_q), .data(rom_1_data), .sel(clock_1_out));
  Pull_Resistor pull_resistor_1 (.node(rom_1_data));
  Counter #(.width(4), .max('hf)) counter_1 (
    .count(clock_1_out), .Q(counter_1_q), .clk(clock_1_out), .clr(and_1_out));  // open: load, D, carry
  and and_1 (and_1_out, clock_1_out, rom_1_data[23]);
  ALU_State_Out_Decoder alu_state_out_decoder_1 (
    .State_In(alu_1_alu_state_out), .State_Select(rom_1_data[22:20]),
    .State_out(alu_state_out_decoder_1_state_out));
  Hex_Digit_Display hex_digit_display_1 (.value(out_1[7:4]));  // open: dp
  Counter #(.trigger("falling")) counter_2 (
    .load(rom_1_data[19]), .D(out_1), .count(not_1_out), .Q(counter_2_q), .clk(rom_1_data[18]));  // open: carry, clr
  not not_1 (not_1_out, rom_1_data[19]);
  Register #(.trigger("falling")) register_3 (
    .D(out_1), .en(1'b1), .Q(register_3_q), .clk(rom_1_data[16]));  // open: clr
  assign controlled_buffer_1_out = rom_1_data[15] ? out_1 : 8'bz;  // Controlled_Buffer controlled_buffer_1
  RAM ram_1 (
    .addr(register_3_q), .data(controlled_buffer_1_out), .sel(1'b1), .clk(rom_1_data[15]), .ld(rom_1_data[14]));  // open: clr
  Hex_Digit_Display hex_digit_display_2 (.value(internal_screen_1__2_digit));  // open: dp
  Internal_Screen internal_screen_1 (
    .\input (out_1), ._1_digit(internal_screen_1__1_digit), ._2_digit(internal_screen_1__2_digit),
    .Update_Values(rom_1_data[13]));
  Hex_Digit_Display hex_digit_display_3 (.value(internal_screen_1__1_digit));  // open: dp
  Hex_Digit_Display hex_digit_display_4 (.value(out_1[3:0]));  // open: dp
  assign out_1 = rom_1_data[4] ? X_Register_q : 8'bz;  // Controlled_Buffer controlled_buffer_2
  assign out_1 = rom_1_data[17] ? counter_2_q : 8'bz;  // Controlled_Buffer controlled_buffer_3
  assign out_1 = rom_1_data[8] ? A_Register_q : 8'bz;  // Controlled_Buffer controlled_buffer_4
  assign out_1 = rom_1_data[14] ? controlled_buffer_1_out : 8'bz;  // Controlled_Buffer controlled_buffer_5
  assign out_1 = rom_1_data[10] ? B_Register_q : 8'bz;  // Controlled_Buffer controlled_buffer_6
  Register X_Register (.D(out_1), .en(1'b1), .Q(X_Register_q), .clk(rom_1_data[3]));  // open: clr
  Register Y_Register (.D(out_1), .en(1'b1), .Q(Y_Register_q), .clk(rom_1_data[5]));  // open: clr
  assign out_1 = rom_1_data[6] ? Y_Register_q : 8'bz;  // Controlled_Buffer controlled_buffer_7
  Register A_Register (.D(out_1), .en(1'b1), .Q(A_Register_q), .clk(rom_1_data[7]), .clr(rom_1_data[7]));
  ALU alu_1 (
    .A_Input(A_Register_q), .B_Input(B_Register_q), .ALU_State_IN(rom_1_data[2:0]), .ALU_Out(out_1),
    .ALU_State_Out(alu_1_alu_state_out));
  Register B_Register (.D(out_1), .en(1'b1), .Q(B_Register_q), .clk(rom_1_data[9]));  // open: clr
  Register Jump_Register (.D(out_1), .en(1'b1), .Q(Jump_Register_q), .clk(rom_1_data[11]));  // open: clr
  assign out_1 = rom_1_data[12] ? Jump_Register_q : 8'bz;  // Controlled_Buffer controlled_buffer_8

  // Notes on the sheet:
  //   contents of rom_1 (hex, n*v repeats v):
  //   30000 1044000 800000 3325*0 30000 1044000 2100 800000 12*0 30000 1044000 2010 800000 12*0 30000
  //   1044000 2040 800000
endmodule

module ALU (
  input  [7:0] A_Input,
  input  [7:0] B_Input,
  input  [2:0] ALU_State_IN,
  output [7:0] ALU_Out,
  output [3:0] ALU_State_Out
);

  wire demultiplexer_1_out1, demultiplexer_1_out2, demultiplexer_1_out3, demultiplexer_1_out4,
       demultiplexer_1_out5, demultiplexer_1_out6, demultiplexer_1_out7;
  wire [7:0] adder_1_out, divider_1_out, multiplier_1_out, subtractor_1_out;

  Pull_Resistor pull_resistor_1 (.node(A_Input));
  Pull_Resistor pull_resistor_2 (.node(B_Input));
  Pull_Resistor pull_resistor_3 (.node(ALU_State_IN));
  Demultiplexer #(.select(3), .disabled(0)) demultiplexer_1 (
    .out1(demultiplexer_1_out1), .out2(demultiplexer_1_out2), .out3(demultiplexer_1_out3),
    .out4(demultiplexer_1_out4), .out5(demultiplexer_1_out5), .out6(demultiplexer_1_out6),
    .out7(demultiplexer_1_out7), .sel(ALU_State_IN), .en(1'b1));  // open: out0, in
  Adder adder_1 (.a(A_Input), .b(B_Input), .out(adder_1_out), .cout(ALU_State_Out[0]));  // open: cin
  assign ALU_Out = demultiplexer_1_out1 ? adder_1_out : 8'bz;  // Controlled_Buffer controlled_buffer_1
  Subtractor subtractor_1 (.a(A_Input), .b(B_Input), .out(subtractor_1_out));  // open: bin, bout
  assign ALU_Out = demultiplexer_1_out2 ? subtractor_1_out : 8'bz;  // Controlled_Buffer controlled_buffer_2
  assign ALU_Out = demultiplexer_1_out3 ? multiplier_1_out : 8'bz;  // Controlled_Buffer controlled_buffer_3
  Multiplier multiplier_1 (.a(A_Input), .b(B_Input), .out(multiplier_1_out));  // open: cin, cout
  Divider divider_1 (.a(A_Input), .b(B_Input), .out(divider_1_out));  // open: upper, rem
  assign ALU_Out = demultiplexer_1_out4 ? divider_1_out : 8'bz;  // Controlled_Buffer controlled_buffer_4
  assign ALU_Out = demultiplexer_1_out5 ? {A_Input[6:0], 1'b0} : 8'bz;  // Controlled_Buffer controlled_buffer_5
  assign ALU_Out = demultiplexer_1_out6 ? {1'b0, A_Input[7:1]} : 8'bz;  // Controlled_Buffer controlled_buffer_6
  assign ALU_Out = demultiplexer_1_out7 ? A_Input : 8'bz;  // Controlled_Buffer controlled_buffer_7
  Comparator comparator_1 (
    .a(A_Input), .b(B_Input), .gt(ALU_State_Out[1]), .eq(ALU_State_Out[2]), .lt(ALU_State_Out[3]));
endmodule

// 0
module ALU_State_Out_Decoder (
  input  [3:0] State_In,
  input  [2:0] State_Select,
  output [3:0] State_out
);

  wire bitselector_1_out, comparator_1_eq, not_1_out;
  wire [2:0] subtractor_1_out;
  wire [3:0] demultiplexer_1_out0;

  Demultiplexer #(.select(3), .disabled(0)) demultiplexer_1 (
    .out0(demultiplexer_1_out0[0]), .out1(demultiplexer_1_out0[1]), .out2(demultiplexer_1_out0[2]),
    .out3(demultiplexer_1_out0[3]), .in(bitselector_1_out), .sel(subtractor_1_out));  // open: out4, out5, out6, out7, en
  BitSelector #(.width(5)) bitselector_1 (.in({1'b0, State_In}), .out(bitselector_1_out), .sel(subtractor_1_out));
  Subtractor #(.width(3)) subtractor_1 (.a(State_Select), .b(3'b001), .out(subtractor_1_out));  // open: bin, bout
  Comparator #(.width(3)) comparator_1 (.a(State_Select), .b(3'b000), .eq(comparator_1_eq));  // open: gt, lt
  not not_1 (not_1_out, comparator_1_eq);
  Pull_Resistor pull_resistor_1 (.node(State_out));
  assign State_out = not_1_out ? demultiplexer_1_out0 : 4'bz;  // Controlled_Buffer controlled_buffer_1
endmodule

module Internal_Screen (
  input  [7:0] \input ,
  input  Update_Values,
  output [3:0] _1_digit,
  output [3:0] _2_digit
);

  Register #(.trigger("falling")) register_1 (
    .D(\input ), .en(1'b1), .Q({_2_digit, _1_digit}), .clk(Update_Values));  // open: clr
endmodule
