// Logisim project My CPU Part 18.circ as structural Verilog: 6 circuits, main circuit main
module main (
  input  in_1,
  output [7:0] out_2,
  output [3:0] out_3
);

  wire and_1_out, clock_1_out;
  wire [3:0] alu_state_out_decoder_1_state_out, counter_1_q, internal_screen_1__1_digit,
       internal_screen_1__2_digit, n4_bit_register_1_out_4, register_1_out_4;
  wire [7:0] A_Register_q, B_Register_q, controlled_buffer_1_out, counter_2_q, Jump_Register_q, register_2_q,
       X_Register_q, Y_Register_q;
  wire [7:4] register_1_out_4_2;
  wire [31:0] rom_1_data;

  Hex_Digit_Display hex_digit_display_1 (.value(register_1_out_4_2));  // open: dp
  Hex_Digit_Display hex_digit_display_2 (.value(n4_bit_register_1_out_4));  // open: dp
  Hex_Digit_Display hex_digit_display_3 (.value(counter_1_q));  // open: dp
  Hex_Digit_Display hex_digit_display_4 (.value(register_1_out_4));  // open: dp
  Register register_1 (
    .in_1(out_2), .Enable(in_1), .clock(rom_1_data[24]), .out_4({register_1_out_4_2, register_1_out_4}));
  _4_Bit_Register u_4_bit_register_1 (
    .in_1(alu_state_out_decoder_1_state_out), .Enable(rom_1_data[26]), .clock(in_1),
    .out_4(n4_bit_register_1_out_4));
  Clock clock_1 (.out(clock_1_out));
  ROM #(.addrWidth(16), .dataWidth(32)) rom_1 (
    .addr({n4_bit_register_1_out_4, register_1_out_4_2, register_1_out_4, counter_1_q}), .data(rom_1_data),
    .sel(in_1));
  Pull_Resistor pull_resistor_1 (.node(rom_1_data));
  Counter #(.width(4), .max('hf), .trigger("falling")) counter_1 (
    .count(1'b1), .Q(counter_1_q), .clk(clock_1_out), .clr(and_1_out));  // open: load, D, carry
  and and_1 (and_1_out, clock_1_out, rom_1_data[23]);
  ALU_State_Out_Decoder alu_state_out_decoder_1 (
    .State_In(out_3), .State_Select(rom_1_data[22:20]), .State_out(alu_state_out_decoder_1_state_out));
  Hex_Digit_Display hex_digit_display_5 (.value(rom_1_data[3:0]));  // open: dp
  Hex_Digit_Display hex_digit_display_6 (.value(rom_1_data[7:4]));  // open: dp
  Hex_Digit_Display hex_digit_display_7 (.value(rom_1_data[11:8]));  // open: dp
  Hex_Digit_Display hex_digit_display_8 (.value(rom_1_data[19:16]));  // open: dp
  Hex_Digit_Display hex_digit_display_9 (.value(rom_1_data[15:12]));  // open: dp
  Hex_Digit_Display hex_digit_display_10 (.value(rom_1_data[27:24]));  // open: dp
  Hex_Digit_Display hex_digit_display_11 (.value(rom_1_data[23:20]));  // open: dp
  Hex_Digit_Display hex_digit_display_12 (.value(out_2[7:4]));  // open: dp
  Counter #(.trigger("falling")) counter_2 (
    .load(rom_1_data[19]), .D(out_2), .count(rom_1_data[18]), .Q(counter_2_q), .clk(clock_1_out), .clr(in_1));  // open: carry
  Register_part #(.trigger("falling")) register_2 (
    .D(out_2), .en(1'b1), .Q(register_2_q), .clk(rom_1_data[16]), .clr(in_1));
  assign controlled_buffer_1_out = rom_1_data[15] ? out_2 : 8'bz;  // Controlled_Buffer controlled_buffer_1
  RAM ram_1 (
    .addr(register_2_q), .data(controlled_buffer_1_out), .sel(1'b1), .clk(rom_1_data[15]), .ld(rom_1_data[14]));  // open: clr
  Internal_Screen internal_screen_1 (
    .\input (out_2), ._1_digit(internal_screen_1__1_digit), ._2_digit(internal_screen_1__2_digit),
    .Update_Values(rom_1_data[13]));
  Hex_Digit_Display hex_digit_display_13 (.value(internal_screen_1__1_digit));  // open: dp
  Hex_Digit_Display hex_digit_display_14 (.value(internal_screen_1__2_digit));  // open: dp
  Hex_Digit_Display hex_digit_display_15 (.value(rom_1_data[31:28]));  // open: dp
  Hex_Digit_Display hex_digit_display_16 (.value(out_2[3:0]));  // open: dp
  Pull_Resistor pull_resistor_2 (.node(out_2));
  assign out_2 = rom_1_data[17] ? counter_2_q : 8'bz;  // Controlled_Buffer controlled_buffer_2
  assign out_2 = rom_1_data[4] ? X_Register_q : 8'bz;  // Controlled_Buffer controlled_buffer_3
  assign out_2 = rom_1_data[8] ? A_Register_q : 8'bz;  // Controlled_Buffer controlled_buffer_4
  assign out_2 = rom_1_data[14] ? controlled_buffer_1_out : 8'bz;  // Controlled_Buffer controlled_buffer_5
  assign out_2 = rom_1_data[10] ? B_Register_q : 8'bz;  // Controlled_Buffer controlled_buffer_6
  Register_part X_Register (.D(out_2), .en(1'b1), .Q(X_Register_q), .clk(rom_1_data[3]));  // open: clr
  Register_part Y_Register (.D(out_2), .en(1'b1), .Q(Y_Register_q), .clk(rom_1_data[5]));  // open: clr
  assign out_2 = rom_1_data[6] ? Y_Register_q : 8'bz;  // Controlled_Buffer controlled_buffer_7
  Register_part #(.trigger("falling")) A_Register (
    .D(out_2), .en(1'b1), .Q(A_Register_q), .clk(rom_1_data[7]));  // open: clr
  ALU alu_1 (
    .A_Input(A_Register_q), .B_Input(B_Register_q), .ALU_State_IN(rom_1_data[2:0]), .ALU_Out(out_2),
    .ALU_State_Out(out_3));
  Register_part B_Register (.D(out_2), .en(1'b1), .Q(B_Register_q), .clk(rom_1_data[9]));  // open: clr
  Register_part Jump_Register (.D(out_2), .en(1'b1), .Q(Jump_Register_q), .clk(rom_1_data[11]));  // open: clr
  assign out_2 = rom_1_data[12] ? Jump_Register_q : 8'bz;  // Controlled_Buffer controlled_buffer_8

  // Notes on the sheet:
  //   contents of rom_1 (hex, n*v repeats v):
  //   30000 1044000 800000 2557*0 30000 1044000 30000 84000 800000 11*0 30000 1044000 30000 84000 800000
  //   11*0 30000 1044000 340000 300000 300000 300000 800000 473*0 30000 1044000 81 800000 252*0 30000
  //   1044000 2100 800000 12*0 30000 1044000 2010 800000 12*0 30000 1044000 2040 800000 13023*0 300000
  //   2590*0 300000 330000 384000 b00000
endmodule

module ALU (
  input  [7:0] A_Input,
  input  [7:0] B_Input,
  input  [2:0] ALU_State_IN,
  output [7:0] ALU_Out,
  output [3:0] ALU_State_Out
);

  wire demultiplexer_1_out1, demultiplexer_1_out2, demultiplexer_1_out3, demultiplexer_1_out4,
       demultiplexer_1_out5, demultiplexer_1_out6, demultiplexer_1_out7;
  wire [7:0] adder_1_out, divider_1_out, multiplier_1_out, subtractor_1_out;

  Pull_Resistor pull_resistor_1 (.node(A_Input));
  Pull_Resistor pull_resistor_2 (.node(B_Input));
  Pull_Resistor pull_resistor_3 (.node(ALU_State_IN));
  Demultiplexer #(.select(3), .disabled(0)) demultiplexer_1 (
    .out1(demultiplexer_1_out1), .out2(demultiplexer_1_out2), .out3(demultiplexer_1_out3),
    .out4(demultiplexer_1_out4), .out5(demultiplexer_1_out5), .out6(demultiplexer_1_out6),
    .out7(demultiplexer_1_out7), .in(1'b1), .sel(ALU_State_IN), .en(1'b1));  // open: out0
  Adder adder_1 (.a(A_Input), .b(B_Input), .out(adder_1_out), .cout(ALU_State_Out[0]));  // open: cin
  assign ALU_Out = demultiplexer_1_out1 ? adder_1_out : 8'bz;  // Controlled_Buffer controlled_buffer_1
  Subtractor subtractor_1 (.a(A_Input), .b(B_Input), .out(subtractor_1_out));  // open: bin, bout
  assign ALU_Out = demultiplexer_1_out2 ? subtractor_1_out : 8'bz;  // Controlled_Buffer controlled_buffer_2
  Multiplier multiplier_1 (.a(A_Input), .b(B_Input), .out(multiplier_1_out));  // open: cin, cout
  assign ALU_Out = demultiplexer_1_out3 ? multiplier_1_out : 8'bz;  // Controlled_Buffer controlled_buffer_3
  assign ALU_Out = demultiplexer_1_out4 ? divider_1_out : 8'bz;  // Controlled_Buffer controlled_buffer_4
  Divider divider_1 (.a(A_Input), .b(B_Input), .out(divider_1_out));  // open: upper, rem
  assign ALU_Out = demultiplexer_1_out5 ? {A_Input[6:0], 1'b0} : 8'bz;  // Controlled_Buffer controlled_buffer_5
  assign ALU_Out = demultiplexer_1_out6 ? {1'b0, A_Input[7:1]} : 8'bz;  // Controlled_Buffer controlled_buffer_6
  assign ALU_Out = demultiplexer_1_out7 ? A_Input : 8'bz;  // Controlled_Buffer controlled_buffer_7
  Comparator comparator_1 (
    .a(A_Input), .b(B_Input), .gt(ALU_State_Out[1]), .eq(ALU_State_Out[2]), .lt(ALU_State_Out[3]));
endmodule

// 0
module ALU_State_Out_Decoder (
  input  [3:0] State_In,
  input  [2:0] State_Select,
  output [3:0] State_out
);

  wire bitselector_1_out, comparator_1_eq, not_1_out;
  wire [2:0] subtractor_1_out;
  wire [3:0] demultiplexer_1_out0;

  BitSelector #(.width(5)) bitselector_1 (.in({1'b0, State_In}), .out(bitselector_1_out), .sel(subtractor_1_out));
  Demultiplexer #(.select(3), .disabled(0)) demultiplexer_1 (
    .out0(demultiplexer_1_out0[0]), .out1(demultiplexer_1_out0[1]), .out2(demultiplexer_1_out0[2]),
    .out3(demultiplexer_1_out0[3]), .in(bitselector_1_out), .sel(subtractor_1_out));  // open: out4, out5, out6, out7, en
  Subtractor #(.width(3)) subtractor_1 (.a(State_Select), .b(3'b001), .out(subtractor_1_out));  // open: bin, bout
  Comparator #(.width(3)) comparator_1 (.a(State_Select), .b(3'b000), .eq(comparator_1_eq));  // open: gt, lt
  not not_1 (not_1_out, comparator_1_eq);
  Pull_Resistor pull_resistor_1 (.node(State_out));
  assign State_out = not_1_out ? demultiplexer_1_out0 : 4'bz;  // Controlled_Buffer controlled_buffer_1
endmodule

module Internal_Screen (
  input  [7:0] \input ,
  input  Update_Values,
  output [3:0] _1_digit,
  output [3:0] _2_digit
);

  Register_part #(.trigger("falling")) register_1 (
    .D(\input ), .en(1'b1), .Q({_2_digit, _1_digit}), .clk(Update_Values));  // open: clr
endmodule

module Register (
  input  [7:0] in_1,
  input  Enable,
  input  clock,
  output [7:0] out_4
);

  Register_part #(.trigger("falling")) register_1 (.D(in_1), .en(Enable), .Q(out_4), .clk(clock));  // open: clr
endmodule

module _4_Bit_Register (
  input  [3:0] in_1,
  input  Enable,
  input  clock,
  output [3:0] out_4
);

  Register_part #(.width(4), .trigger("falling")) register_1 (
    .D(in_1), .en(Enable), .Q(out_4), .clk(clock));  // open: clr
endmodule
