// Logisim project My CPU Part 2.circ as structural Verilog: 2 circuits, main circuit main
module main (
);

  wire not_1_out, undriven, undriven_2, undriven_3, undriven_4, undriven_5, undriven_6, undriven_7,
       undriven_8, undriven_9, undriven_10;
  wire [3:0] alu_1_alu_state_out;
  wire [7:0] controlled_buffer_1_out, counter_1_q, ram_1_data, register_1_q, register_2_q, register_3_q,
       register_4_q, register_5_q;

  Hex_Digit_Display hex_digit_display_1 ();  // open: value, dp
  not not_1 (not_1_out, undriven_3);
  Register register_1 (.D(controlled_buffer_1_out), .en(1'b1), .Q(register_1_q), .clk(undriven));  // open: clr
  RAM ram_1 (.addr(register_1_q), .data(ram_1_data), .sel(1'b1), .clk(undriven_2), .ld(undriven_6));  // open: clr
  Hex_Digit_Display hex_digit_display_2 ();  // open: value, dp
  Hex_Digit_Display hex_digit_display_3 ();  // open: value, dp
  Counter counter_1 (
    .load(undriven_3), .D(controlled_buffer_1_out), .count(not_1_out), .Q(counter_1_q), .clk(undriven_4));  // open: carry, clr
  assign controlled_buffer_1_out = undriven_5 ? counter_1_q : 8'bz;  // Controlled_Buffer controlled_buffer_1
  assign ram_1_data = undriven_2 ? controlled_buffer_1_out : 8'bz;  // Controlled_Buffer controlled_buffer_2
  assign controlled_buffer_1_out = undriven_6 ? ram_1_data : 8'bz;  // Controlled_Buffer controlled_buffer_3
  Register register_2 (.D(controlled_buffer_1_out), .en(1'b1), .Q(register_2_q));  // open: clk, clr
  assign controlled_buffer_1_out = undriven_7 ? register_2_q : 8'bz;  // Controlled_Buffer controlled_buffer_4
  Register register_3 (.D(controlled_buffer_1_out), .en(1'b1), .Q(register_3_q));  // open: clk, clr
  assign controlled_buffer_1_out = undriven_8 ? register_3_q : 8'bz;  // Controlled_Buffer controlled_buffer_5
  Register register_4 (.D(controlled_buffer_1_out), .en(1'b1), .Q(register_4_q), .clk(undriven_9));  // open: clr
  ALU alu_1 (
    .A_Input(register_4_q), .B_Input(register_5_q), .ALU_Out(controlled_buffer_1_out),
    .ALU_State_Out(alu_1_alu_state_out));  // open: ALU_State_IN
  Register register_5 (.D(controlled_buffer_1_out), .en(1'b1), .Q(register_5_q), .clk(undriven_10));  // open: clr
endmodule

module ALU (
  input  [7:0] A_Input,
  input  [7:0] B_Input,
  input  [2:0] ALU_State_IN,
  output [7:0] ALU_Out,
  output [3:0] ALU_State_Out
);

  wire demultiplexer_1_out1, demultiplexer_1_out2, demultiplexer_1_out3, demultiplexer_1_out4,
       demultiplexer_1_out5, demultiplexer_1_out6, demultiplexer_1_out7;
  wire [7:0] adder_1_out, divider_1_out, multiplier_1_out, subtractor_1_out;

  Pull_Resistor pull_resistor_1 (.node(A_Input));
  Pull_Resistor pull_resistor_2 (.node(B_Input));
  Pull_Resistor pull_resistor_3 (.node(ALU_State_IN));
  Demultiplexer #(.select(3), .disabled(0)) demultiplexer_1 (
    .out1(demultiplexer_1_out1), .out2(demultiplexer_1_out2), .out3(demultiplexer_1_out3),
    .out4(demultiplexer_1_out4), .out5(demultiplexer_1_out5), .out6(demultiplexer_1_out6),
    .out7(demultiplexer_1_out7), .sel(ALU_State_IN), .en(1'b1));  // open: out0, in
  Pull_Resistor pull_resistor_4 (.node(ALU_Out));
  Adder adder_1 (.a(A_Input), .b(B_Input), .out(adder_1_out), .cout(ALU_State_Out[0]));  // open: cin
  assign ALU_Out = demultiplexer_1_out1 ? adder_1_out : 8'bz;  // Controlled_Buffer controlled_buffer_1
  assign ALU_Out = demultiplexer_1_out2 ? subtractor_1_out : 8'bz;  // Controlled_Buffer controlled_buffer_2
  Subtractor subtractor_1 (.a(A_Input), .b(B_Input), .out(subtractor_1_out));  // open: bin, bout
  Multiplier multiplier_1 (.a(A_Input), .b(B_Input), .out(multiplier_1_out));  // open: cin, cout
  assign ALU_Out = demultiplexer_1_out3 ? multiplier_1_out : 8'bz;  // Controlled_Buffer controlled_buffer_3
  assign ALU_Out = demultiplexer_1_out4 ? divider_1_out : 8'bz;  // Controlled_Buffer controlled_buffer_4
  Divider divider_1 (.a(A_Input), .b(B_Input), .out(divider_1_out));  // open: upper, rem
  assign ALU_Out = demultiplexer_1_out5 ? {A_Input[6:0], 1'b0} : 8'bz;  // Controlled_Buffer controlled_buffer_5
  assign ALU_Out = demultiplexer_1_out6 ? {1'b0, A_Input[7:1]} : 8'bz;  // Controlled_Buffer controlled_buffer_6
  assign ALU_Out = demultiplexer_1_out7 ? A_Input : 8'bz;  // Controlled_Buffer controlled_buffer_7
  Comparator comparator_1 (
    .a(A_Input), .b(B_Input), .gt(ALU_State_Out[1]), .eq(ALU_State_Out[2]), .lt(ALU_State_Out[3]));
endmodule
