// Logisim project My CPU Part 26(16 bits!!!).circ as structural Verilog: 7 circuits, main circuit main
module main (
  input  reset,
  input  in_2,
  output [3:0] out_3
);

  wire clock_1_out, clock_2_out, cpu_1_read, cpu_1_write, or_1_out;
  wire [3:0] alu_state_out_decoder_1_state_out, counter_1_q, internal_screen_1__1_digit,
       internal_screen_1__2_digit, internal_screen_1__3_digit, internal_screen_1__4_digit,
       pull_resistor_2_node, pull_resistor_2_node_2, pull_resistor_2_node_3, pull_resistor_2_node_4,
       register_1_out_4;
  wire [7:4] register_1_out_4_2;
  wire [15:0] A_Register_q, B_Register_q, controlled_buffer_1_out, controlled_buffer_2_out, counter_2_q,
       cpu_1_address, Jump_Register_q, ram_2_data, register_2_q, X_Register_q, Y_Register_q;
  wire [31:0] pull_resistor_1_node;

  Hex_Digit_Display hex_digit_display_1 (.value(alu_state_out_decoder_1_state_out));  // open: dp
  Hex_Digit_Display hex_digit_display_2 (.value(register_1_out_4_2));  // open: dp
  Hex_Digit_Display hex_digit_display_3 (.value(register_1_out_4));  // open: dp
  Hex_Digit_Display hex_digit_display_4 (.value(counter_1_q));  // open: dp
  assign controlled_buffer_1_out = clock_1_out ? {alu_state_out_decoder_1_state_out, register_1_out_4_2, register_1_out_4, counter_1_q} : 16'bz;  // Controlled_Buffer controlled_buffer_1
  Clock clock_1 (.out(clock_1_out));
  Pull_Resistor pull_resistor_1 (.node(pull_resistor_1_node));
  Register register_1 (
    .in_1({pull_resistor_2_node_4, pull_resistor_2_node_3, pull_resistor_2_node_2, pull_resistor_2_node}),
    .Enable(pull_resistor_1_node[24]), .out_4({register_1_out_4_2, register_1_out_4}), .reset(reset));
  ROM #(.addrWidth(16), .dataWidth(32)) rom_1 (
    .addr(controlled_buffer_1_out), .data(pull_resistor_1_node), .sel(clock_1_out));
  Hex_Digit_Display hex_digit_display_5 (.value(pull_resistor_1_node[27:24]));  // open: dp
  Hex_Digit_Display hex_digit_display_6 (.value(pull_resistor_1_node[31:28]));  // open: dp
  Counter #(.width(4), .max('hf), .trigger("falling")) counter_1 (
    .count(1'b1), .Q(counter_1_q), .clk(clock_1_out), .clr(or_1_out));  // open: load, D, carry
  or or_1 (or_1_out, reset, pull_resistor_1_node[23]);
  ALU_State_Out_Decoder alu_state_out_decoder_1 (
    .State_In(out_3), .State_Select(pull_resistor_1_node[22:20]),
    .State_out(alu_state_out_decoder_1_state_out), .reset(or_1_out));
  Hex_Digit_Display hex_digit_display_7 (.value(pull_resistor_1_node[23:20]));  // open: dp
  Hex_Digit_Display hex_digit_display_8 (.value(pull_resistor_1_node[19:16]));  // open: dp
  Register_part #(.width(16), .trigger("falling")) register_2 (
    .D({pull_resistor_2_node_4, pull_resistor_2_node_3, pull_resistor_2_node_2, pull_resistor_2_node}),
    .en(1'b1), .Q(register_2_q), .clk(pull_resistor_1_node[16]), .clr(reset));
  Hex_Digit_Display hex_digit_display_9 (.value(pull_resistor_1_node[15:12]));  // open: dp
  Hex_Digit_Display hex_digit_display_10 (.value(pull_resistor_1_node[11:8]));  // open: dp
  Hex_Digit_Display hex_digit_display_11 (.value(pull_resistor_1_node[3:0]));  // open: dp
  Hex_Digit_Display hex_digit_display_12 (.value(pull_resistor_1_node[7:4]));  // open: dp
  Hex_Digit_Display hex_digit_display_13 (.value(pull_resistor_2_node_4));  // open: dp
  Hex_Digit_Display hex_digit_display_14 (.value(pull_resistor_2_node_3));  // open: dp
  Hex_Digit_Display hex_digit_display_15 (.value(internal_screen_1__4_digit));  // open: dp
  Hex_Digit_Display hex_digit_display_16 (.value(internal_screen_1__3_digit));  // open: dp
  Hex_Digit_Display hex_digit_display_17 (.value(pull_resistor_2_node));  // open: dp
  Hex_Digit_Display hex_digit_display_18 (.value(pull_resistor_2_node_2));  // open: dp
  Counter #(.width(16), .max('hffff), .trigger("falling")) counter_2 (
    .load(pull_resistor_1_node[19]),
    .D({pull_resistor_2_node_4, pull_resistor_2_node_3, pull_resistor_2_node_2, pull_resistor_2_node}),
    .count(pull_resistor_1_node[18]), .Q(counter_2_q), .clk(clock_1_out), .clr(reset));  // open: carry
  assign controlled_buffer_2_out = pull_resistor_1_node[15] ? {pull_resistor_2_node_4, pull_resistor_2_node_3, pull_resistor_2_node_2, pull_resistor_2_node} : 16'bz;  // Controlled_Buffer controlled_buffer_2
  RAM #(.addrWidth(16), .dataWidth(16)) ram_1 (
    .addr(register_2_q), .data(controlled_buffer_2_out), .sel(1'b1), .clk(pull_resistor_1_node[15]),
    .ld(pull_resistor_1_node[14]));  // open: clr
  Hex_Digit_Display hex_digit_display_19 (.value(internal_screen_1__2_digit));  // open: dp
  Hex_Digit_Display hex_digit_display_20 (.value(internal_screen_1__1_digit));  // open: dp
  Internal_Screen internal_screen_1 (
    .\input ({pull_resistor_2_node_4, pull_resistor_2_node_3, pull_resistor_2_node_2, pull_resistor_2_node}),
    ._1_digit(internal_screen_1__1_digit), ._2_digit(internal_screen_1__2_digit),
    .Update_Values(pull_resistor_1_node[13]), ._3_digit(internal_screen_1__3_digit),
    ._4_digit(internal_screen_1__4_digit));
  Pull_Resistor pull_resistor_2 (.node({pull_resistor_2_node_4, pull_resistor_2_node_3, pull_resistor_2_node_2, pull_resistor_2_node}));
  assign {pull_resistor_2_node_4, pull_resistor_2_node_3, pull_resistor_2_node_2, pull_resistor_2_node} = pull_resistor_1_node[17] ? counter_2_q : 16'bz;  // Controlled_Buffer controlled_buffer_3
  assign {pull_resistor_2_node_4, pull_resistor_2_node_3, pull_resistor_2_node_2, pull_resistor_2_node} = pull_resistor_1_node[4] ? X_Register_q : 16'bz;  // Controlled_Buffer controlled_buffer_4
  assign {pull_resistor_2_node_4, pull_resistor_2_node_3, pull_resistor_2_node_2, pull_resistor_2_node} = pull_resistor_1_node[14] ? controlled_buffer_2_out : 16'bz;  // Controlled_Buffer controlled_buffer_5
  assign {pull_resistor_2_node_4, pull_resistor_2_node_3, pull_resistor_2_node_2, pull_resistor_2_node} = pull_resistor_1_node[8] ? A_Register_q : 16'bz;  // Controlled_Buffer controlled_buffer_6
  assign {pull_resistor_2_node_4, pull_resistor_2_node_3, pull_resistor_2_node_2, pull_resistor_2_node} = pull_resistor_1_node[10] ? B_Register_q : 16'bz;  // Controlled_Buffer controlled_buffer_7
  Register_part #(.width(16)) X_Register (
    .D({pull_resistor_2_node_4, pull_resistor_2_node_3, pull_resistor_2_node_2, pull_resistor_2_node}),
    .en(1'b1), .Q(X_Register_q), .clk(pull_resistor_1_node[3]));  // open: clr
  Register_part #(.width(16)) Y_Register (
    .D({pull_resistor_2_node_4, pull_resistor_2_node_3, pull_resistor_2_node_2, pull_resistor_2_node}),
    .en(1'b1), .Q(Y_Register_q), .clk(pull_resistor_1_node[5]));  // open: clr
  assign {pull_resistor_2_node_4, pull_resistor_2_node_3, pull_resistor_2_node_2, pull_resistor_2_node} = pull_resistor_1_node[6] ? Y_Register_q : 16'bz;  // Controlled_Buffer controlled_buffer_8
  Register_part #(.width(16), .trigger("falling")) A_Register (
    .D({pull_resistor_2_node_4, pull_resistor_2_node_3, pull_resistor_2_node_2, pull_resistor_2_node}),
    .en(1'b1), .Q(A_Register_q), .clk(pull_resistor_1_node[7]));  // open: clr
  ALU alu_1 (
    .A_Input(A_Register_q), .B_Input(B_Register_q), .ALU_State_IN(pull_resistor_1_node[2:0]),
    .ALU_Out({pull_resistor_2_node_4, pull_resistor_2_node_3, pull_resistor_2_node_2, pull_resistor_2_node}),
    .ALU_State_Out(out_3));
  Register_part #(.width(16)) B_Register (
    .D({pull_resistor_2_node_4, pull_resistor_2_node_3, pull_resistor_2_node_2, pull_resistor_2_node}),
    .en(1'b1), .Q(B_Register_q), .clk(pull_resistor_1_node[9]));  // open: clr
  Register_part #(.width(16), .trigger("falling")) Jump_Register (
    .D({pull_resistor_2_node_4, pull_resistor_2_node_3, pull_resistor_2_node_2, pull_resistor_2_node}),
    .en(1'b1), .Q(Jump_Register_q), .clk(pull_resistor_1_node[11]));  // open: clr
  assign {pull_resistor_2_node_4, pull_resistor_2_node_3, pull_resistor_2_node_2, pull_resistor_2_node} = pull_resistor_1_node[12] ? Jump_Register_q : 16'bz;  // Controlled_Buffer controlled_buffer_9
  RAM #(.addrWidth(16), .dataWidth(16)) ram_2 (
    .addr(cpu_1_address), .data(ram_2_data), .clk(cpu_1_write), .ld(cpu_1_read));  // open: sel, clr
  Clock clock_2 (.out(clock_2_out));
  CPU cpu_1 (
    .reset(in_2), .clock(clock_2_out), .Data(ram_2_data), .Address(cpu_1_address), .Write(cpu_1_write),
    .Read(cpu_1_read));

  // Notes on the sheet:
  //   contents of rom_1 (hex, n*v repeats v):
  //   30000 1044000 800000 2557*0 30000 1044000 30000 84000 800000 11*0 30000 1044000 30000 84000 800000
  //   11*0 30000 1044000 340000 800000 220*0 30000 1044000 30000 60800 84000 800000 58*0 30000 1044000
  //   81000 800000 188*0 30000 1044000 81 800000 12*0 30000 1044000 82 800000 12*0 30000 1044000 83 800000
  //   12*0 30000 1044000 84 800000 12*0 30000 1044000 85 800000 12*0 30000 1044000 86 800000 12*0 30000
  //   1044000 87 800000 156*0 30000 1044000 2100 800000 12*0 30000 1044000 2010 800000 12*0 30000 1044000
  //   2040 800000 12*0 30000 1044000 30000 54000 6000 800000 13005*0 300000 2590*0 300000 330000 384000
  //   b00000
endmodule

module ALU (
  input  [15:0] A_Input,
  input  [15:0] B_Input,
  input  [2:0] ALU_State_IN,
  output [15:0] ALU_Out,
  output [3:0] ALU_State_Out
);

  wire demultiplexer_1_out1, demultiplexer_1_out2, demultiplexer_1_out3, demultiplexer_1_out4,
       demultiplexer_1_out5, demultiplexer_1_out6, demultiplexer_1_out7;
  wire [15:0] adder_1_out, divider_1_out, multiplier_1_out, subtractor_1_out, undriven;

  Pull_Resistor pull_resistor_1 (.node(A_Input));
  Pull_Resistor pull_resistor_2 (.node(B_Input));
  Pull_Resistor pull_resistor_3 (.node(ALU_State_IN));
  Demultiplexer #(.select(3), .disabled(0)) demultiplexer_1 (
    .out1(demultiplexer_1_out1), .out2(demultiplexer_1_out2), .out3(demultiplexer_1_out3),
    .out4(demultiplexer_1_out4), .out5(demultiplexer_1_out5), .out6(demultiplexer_1_out6),
    .out7(demultiplexer_1_out7), .in(1'b1), .sel(ALU_State_IN), .en(1'b1));  // open: out0
  Adder #(.width(16)) adder_1 (.a(A_Input), .b(B_Input), .out(adder_1_out), .cout(ALU_State_Out[0]));  // open: cin
  assign ALU_Out = demultiplexer_1_out1 ? adder_1_out : 16'bz;  // Controlled_Buffer controlled_buffer_1
  Subtractor #(.width(16)) subtractor_1 (.a(A_Input), .b(B_Input), .out(subtractor_1_out));  // open: bin, bout
  assign ALU_Out = demultiplexer_1_out2 ? subtractor_1_out : 16'bz;  // Controlled_Buffer controlled_buffer_2
  assign ALU_Out = demultiplexer_1_out3 ? multiplier_1_out : 16'bz;  // Controlled_Buffer controlled_buffer_3
  Multiplier #(.width(16)) multiplier_1 (.a(A_Input), .b(B_Input), .out(multiplier_1_out));  // open: cin, cout
  Divider #(.width(16)) divider_1 (.a(A_Input), .b(B_Input), .out(divider_1_out));  // open: upper, rem
  assign ALU_Out = demultiplexer_1_out4 ? divider_1_out : 16'bz;  // Controlled_Buffer controlled_buffer_4
  assign ALU_Out = demultiplexer_1_out5 ? undriven : 16'bz;  // Controlled_Buffer controlled_buffer_5
  Controlled_Buffer #(.width(16)) controlled_buffer_6 (.out(ALU_Out), .en(demultiplexer_1_out6));  // open: in
  assign ALU_Out = demultiplexer_1_out7 ? A_Input : 16'bz;  // Controlled_Buffer controlled_buffer_7
  Comparator #(.width(16)) comparator_1 (
    .a(A_Input), .b(B_Input), .gt(ALU_State_Out[1]), .eq(ALU_State_Out[2]), .lt(ALU_State_Out[3]));
endmodule

// 0
module ALU_State_Out_Decoder (
  input  [3:0] State_In,
  input  reset,
  input  [2:0] State_Select,
  output [3:0] State_out
);

  wire bitselector_1_out, bitselector_2_out;
  wire [2:0] subtractor_1_out;
  wire [3:0] demultiplexer_1_out0;

  Demultiplexer #(.select(3), .disabled(0)) demultiplexer_1 (
    .out0(demultiplexer_1_out0[0]), .out1(demultiplexer_1_out0[1]), .out2(demultiplexer_1_out0[2]),
    .out3(demultiplexer_1_out0[3]), .in(bitselector_1_out), .sel(subtractor_1_out));  // open: out4, out5, out6, out7, en
  BitSelector #(.width(5)) bitselector_1 (.in({1'b0, State_In}), .out(bitselector_1_out), .sel(subtractor_1_out));
  Subtractor #(.width(3)) subtractor_1 (.a(State_Select), .b(3'b001), .out(subtractor_1_out));  // open: bin, bout
  Comparator #(.width(3)) comparator_1 (.a(State_Select), .b(3'b000));  // open: gt, eq, lt
  Clock clock_1 ();  // open: out
  BitSelector #(.width(4)) bitselector_2 (
    .in(demultiplexer_1_out0), .out(bitselector_2_out), .sel(subtractor_1_out[1:0]));
  Register_part #(.width(4)) register_1 (
    .D(demultiplexer_1_out0), .en(1'b1), .Q(State_out), .clk(bitselector_2_out), .clr(reset));
endmodule

module Internal_Screen (
  input  [15:0] \input ,
  input  Update_Values,
  output [3:0] _1_digit,
  output [3:0] _2_digit,
  output [3:0] _3_digit,
  output [3:0] _4_digit
);

  Register_part #(.width(16), .trigger("falling")) register_1 (
    .D(\input ), .en(1'b1), .Q({_4_digit, _3_digit, _2_digit, _1_digit}), .clk(Update_Values));  // open: clr
endmodule

module Register (
  input  [15:0] in_1,
  input  Enable,
  input  reset,
  output [7:0] out_4
);

  Register_part #(.trigger("falling")) register_1 (.D(in_1[15:8]), .en(1'b1), .Q(out_4), .clk(Enable), .clr(reset));
endmodule

module _4_Bit_Register (
  input  [3:0] in_1,
  input  Enable,
  input  clock,
  input  reset,
  output [3:0] out_5
);

  Register_part #(.width(4), .trigger("falling")) register_1 (
    .D(in_1), .en(Enable), .Q(out_5), .clk(clock), .clr(reset));
endmodule

module CPU (
  input  reset,
  input  clock,
  input  [15:0] Data,
  output [15:0] Address,
  output Write,
  output Read
);

  wire or_1_out;
  wire [3:0] alu_1_alu_state_out, alu_state_out_decoder_1_state_out, counter_1_q, internal_screen_1__1_digit,
       internal_screen_1__2_digit, internal_screen_1__3_digit, internal_screen_1__4_digit,
       pull_resistor_2_node, pull_resistor_2_node_2, pull_resistor_2_node_3, pull_resistor_2_node_4,
       register_1_out_4;
  wire [7:4] register_1_out_4_2;
  wire [15:0] A_Register_q, B_Register_q, controlled_buffer_1_out, counter_2_q, Jump_Register_q,
       X_Register_q, Y_Register_q;
  wire [31:0] pull_resistor_1_node;

  Hex_Digit_Display hex_digit_display_1 (.value(alu_state_out_decoder_1_state_out));  // open: dp
  Hex_Digit_Display hex_digit_display_2 (.value(register_1_out_4_2));  // open: dp
  Hex_Digit_Display hex_digit_display_3 (.value(register_1_out_4));  // open: dp
  assign controlled_buffer_1_out = clock ? {alu_state_out_decoder_1_state_out, register_1_out_4_2, register_1_out_4, counter_1_q} : 16'bz;  // Controlled_Buffer controlled_buffer_1
  Hex_Digit_Display hex_digit_display_4 (.value(counter_1_q));  // open: dp
  Pull_Resistor pull_resistor_1 (.node({pull_resistor_1_node[31:16], Write, Read, pull_resistor_1_node[13:0]}));
  Register register_1 (
    .in_1({pull_resistor_2_node_4, pull_resistor_2_node_3, pull_resistor_2_node_2, pull_resistor_2_node}),
    .Enable(pull_resistor_1_node[24]), .out_4({register_1_out_4_2, register_1_out_4}), .reset(reset));
  ROM #(.addrWidth(16), .dataWidth(32)) rom_1 (
    .addr(controlled_buffer_1_out),
    .data({pull_resistor_1_node[31:16], Write, Read, pull_resistor_1_node[13:0]}), .sel(clock));
  Hex_Digit_Display hex_digit_display_5 (.value(pull_resistor_1_node[31:28]));  // open: dp
  Counter #(.width(4), .max('hf), .trigger("falling")) counter_1 (
    .count(1'b1), .Q(counter_1_q), .clk(clock), .clr(or_1_out));  // open: load, D, carry
  or or_1 (or_1_out, reset, pull_resistor_1_node[23]);
  ALU_State_Out_Decoder alu_state_out_decoder_1 (
    .State_In(alu_1_alu_state_out), .State_Select(pull_resistor_1_node[22:20]),
    .State_out(alu_state_out_decoder_1_state_out), .reset(or_1_out));
  Hex_Digit_Display hex_digit_display_6 (.value(pull_resistor_1_node[23:20]));  // open: dp
  Hex_Digit_Display hex_digit_display_7 (.value(pull_resistor_1_node[27:24]));  // open: dp
  Register_part #(.width(16), .trigger("falling")) register_2 (
    .D({pull_resistor_2_node_4, pull_resistor_2_node_3, pull_resistor_2_node_2, pull_resistor_2_node}),
    .Q(Address), .clk(pull_resistor_1_node[16]), .clr(reset));  // open: en
  Hex_Digit_Display hex_digit_display_8 (.value(pull_resistor_1_node[19:16]));  // open: dp
  Hex_Digit_Display hex_digit_display_9 (.value({Write, Read, pull_resistor_1_node[13:12]}));  // open: dp
  Hex_Digit_Display hex_digit_display_10 (.value(pull_resistor_1_node[11:8]));  // open: dp
  Hex_Digit_Display hex_digit_display_11 (.value(pull_resistor_1_node[7:4]));  // open: dp
  Hex_Digit_Display hex_digit_display_12 (.value(pull_resistor_2_node_4));  // open: dp
  Hex_Digit_Display hex_digit_display_13 (.value(internal_screen_1__4_digit));  // open: dp
  Hex_Digit_Display hex_digit_display_14 (.value(pull_resistor_1_node[3:0]));  // open: dp
  Hex_Digit_Display hex_digit_display_15 (.value(pull_resistor_2_node_2));  // open: dp
  Hex_Digit_Display hex_digit_display_16 (.value(pull_resistor_2_node_3));  // open: dp
  Counter #(.width(16), .max('hffff), .trigger("falling")) counter_2 (
    .load(pull_resistor_1_node[19]),
    .D({pull_resistor_2_node_4, pull_resistor_2_node_3, pull_resistor_2_node_2, pull_resistor_2_node}),
    .count(pull_resistor_1_node[18]), .Q(counter_2_q), .clk(clock), .clr(reset));  // open: carry
  Hex_Digit_Display hex_digit_display_17 (.value(internal_screen_1__3_digit));  // open: dp
  Hex_Digit_Display hex_digit_display_18 (.value(internal_screen_1__2_digit));  // open: dp
  Hex_Digit_Display hex_digit_display_19 (.value(pull_resistor_2_node));  // open: dp
  Pull_Resistor pull_resistor_2 (.node({pull_resistor_2_node_4, pull_resistor_2_node_3, pull_resistor_2_node_2, pull_resistor_2_node}));
  assign {pull_resistor_2_node_4, pull_resistor_2_node_3, pull_resistor_2_node_2, pull_resistor_2_node} = pull_resistor_1_node[17] ? counter_2_q : 16'bz;  // Controlled_Buffer controlled_buffer_2
  assign Data = Write ? {pull_resistor_2_node_4, pull_resistor_2_node_3, pull_resistor_2_node_2, pull_resistor_2_node} : 16'bz;  // Controlled_Buffer controlled_buffer_3
  assign {pull_resistor_2_node_4, pull_resistor_2_node_3, pull_resistor_2_node_2, pull_resistor_2_node} = Read ? Data : 16'bz;  // Controlled_Buffer controlled_buffer_4
  Hex_Digit_Display hex_digit_display_20 (.value(internal_screen_1__1_digit));  // open: dp
  Internal_Screen internal_screen_1 (
    .\input ({pull_resistor_2_node_4, pull_resistor_2_node_3, pull_resistor_2_node_2, pull_resistor_2_node}),
    ._1_digit(internal_screen_1__1_digit), ._2_digit(internal_screen_1__2_digit),
    .Update_Values(pull_resistor_1_node[13]), ._3_digit(internal_screen_1__3_digit),
    ._4_digit(internal_screen_1__4_digit));
  Register_part #(.width(16)) X_Register (
    .D({pull_resistor_2_node_4, pull_resistor_2_node_3, pull_resistor_2_node_2, pull_resistor_2_node}),
    .en(1'b1), .Q(X_Register_q), .clk(pull_resistor_1_node[3]));  // open: clr
  assign {pull_resistor_2_node_4, pull_resistor_2_node_3, pull_resistor_2_node_2, pull_resistor_2_node} = pull_resistor_1_node[4] ? X_Register_q : 16'bz;  // Controlled_Buffer controlled_buffer_5
  Register_part #(.width(16)) Y_Register (
    .D({pull_resistor_2_node_4, pull_resistor_2_node_3, pull_resistor_2_node_2, pull_resistor_2_node}),
    .en(1'b1), .Q(Y_Register_q), .clk(pull_resistor_1_node[5]));  // open: clr
  assign {pull_resistor_2_node_4, pull_resistor_2_node_3, pull_resistor_2_node_2, pull_resistor_2_node} = pull_resistor_1_node[6] ? Y_Register_q : 16'bz;  // Controlled_Buffer controlled_buffer_6
  Register_part #(.width(16), .trigger("falling")) A_Register (
    .D({pull_resistor_2_node_4, pull_resistor_2_node_3, pull_resistor_2_node_2, pull_resistor_2_node}),
    .en(1'b1), .Q(A_Register_q), .clk(pull_resistor_1_node[7]));  // open: clr
  assign {pull_resistor_2_node_4, pull_resistor_2_node_3, pull_resistor_2_node_2, pull_resistor_2_node} = pull_resistor_1_node[8] ? A_Register_q : 16'bz;  // Controlled_Buffer controlled_buffer_7
  ALU alu_1 (
    .A_Input(A_Register_q), .B_Input(B_Register_q), .ALU_State_IN(pull_resistor_1_node[2:0]),
    .ALU_Out({pull_resistor_2_node_4, pull_resistor_2_node_3, pull_resistor_2_node_2, pull_resistor_2_node}),
    .ALU_State_Out(alu_1_alu_state_out));
  Register_part #(.width(16)) B_Register (
    .D({pull_resistor_2_node_4, pull_resistor_2_node_3, pull_resistor_2_node_2, pull_resistor_2_node}),
    .en(1'b1), .Q(B_Register_q), .clk(pull_resistor_1_node[9]));  // open: clr
  assign {pull_resistor_2_node_4, pull_resistor_2_node_3, pull_resistor_2_node_2, pull_resistor_2_node} = pull_resistor_1_node[10] ? B_Register_q : 16'bz;  // Controlled_Buffer controlled_buffer_8
  Register_part #(.width(16), .trigger("falling")) Jump_Register (
    .D({pull_resistor_2_node_4, pull_resistor_2_node_3, pull_resistor_2_node_2, pull_resistor_2_node}),
    .en(1'b1), .Q(Jump_Register_q), .clk(pull_resistor_1_node[11]));  // open: clr
  assign {pull_resistor_2_node_4, pull_resistor_2_node_3, pull_resistor_2_node_2, pull_resistor_2_node} = pull_resistor_1_node[12] ? Jump_Register_q : 16'bz;  // Controlled_Buffer controlled_buffer_9

  // Notes on the sheet:
  //   contents of rom_1 (hex, n*v repeats v):
  //   30000 1044000 800000 2557*0 30000 1044000 30000 84000 800000 11*0 30000 1044000 30000 84000 800000
  //   11*0 30000 1044000 340000 800000 220*0 30000 1044000 30000 60800 84000 800000 58*0 30000 1044000
  //   81000 800000 188*0 30000 1044000 81 800000 12*0 30000 1044000 82 800000 12*0 30000 1044000 83 800000
  //   12*0 30000 1044000 84 800000 12*0 30000 1044000 85 800000 12*0 30000 1044000 86 800000 12*0 30000
  //   1044000 87 800000 156*0 30000 1044000 2100 800000 12*0 30000 1044000 2010 800000 12*0 30000 1044000
  //   2040 800000 12*0 30000 1044000 30000 54000 6000 800000 13005*0 300000 2590*0 300000 330000 384000
  //   b00000
endmodule
