// Logisim project My CPU Part 54(GOL Test) (1).circ as structural Verilog: 12 circuits, main circuit main
module main (
  input  in_1,
  input  in_2
);

  wire clock_1_out, cpu_1_letter_write, cpu_1_read, cpu_1_write, input_logic_1_clock_out,
       input_logic_1_enable, input_logic_1_ram_rom_bus_controll_enable,
       memory_control_1_enable___dissable_ram, memory_control_1_enable___dissable_rom,
       memory_location_panal_1__0x_intro, memory_location_panal_1__2a00_2aff_win,
       memory_location_panal_1__100x_del_old_pixel, memory_location_panal_1__200x_calc_new_pixel,
       memory_location_panal_1__300x_write_new_pixel, memory_location_panal_1__400c_move_paddle_input,
       memory_location_panal_1__500x_paddle_collision_detection,
       memory_location_panal_1__600x_wall_collision_detection,
       memory_location_panal_1__700x_brick_collision_detection, memory_location_panal_1__2300_29ff_game_over,
       memory_location_panal_1_ff00_ffef_reading_writting_varables,
       memory_location_panal_1_ffc0_reading_keyboard, memory_location_panal_1_writting_reading_to_screen;
  wire [6:0] keyboard_1_data;
  wire [14:0] memory_control_1_ram_address, memory_control_1_rom_address;
  wire [15:0] cpu_1_address, cpu_1_internal_screen_out, cpu_1_opcode_mic, cpu_1_out, cpu_1_pg_address_look,
       input_logic_1_bus_output, screen_control_logic_1_screen_row_1, screen_control_logic_1_screen_row_1_2,
       screen_control_logic_1_screen_row_2, screen_control_logic_1_screen_row_3,
       screen_control_logic_1_screen_row_4, screen_control_logic_1_screen_row_5,
       screen_control_logic_1_screen_row_6, screen_control_logic_1_screen_row_7,
       screen_control_logic_1_screen_row_8, screen_control_logic_1_screen_row_9,
       screen_control_logic_1_screen_row_a, screen_control_logic_1_screen_row_b,
       screen_control_logic_1_screen_row_c, screen_control_logic_1_screen_row_d,
       screen_control_logic_1_screen_row_e, screen_control_logic_1_screen_row_f;
  wire [31:0] cpu_1_micro_instruction_oc;

  Memory_control memory_control_1 (
    .Address(cpu_1_address), .enable___dissable_memory(input_logic_1_ram_rom_bus_controll_enable),
    .ROM_address(memory_control_1_rom_address),
    .enable___dissable_ROM(memory_control_1_enable___dissable_rom),
    .enable___dissable_RAM(memory_control_1_enable___dissable_ram),
    .RAM_address(memory_control_1_ram_address), .Read(cpu_1_read));
  Keyboard keyboard_1 (
    .clk(input_logic_1_clock_out), .re(input_logic_1_enable), .data(keyboard_1_data));  // open: clr, avail
  Screen_Control_logic screen_control_logic_1 (
    .Screen_Update(cpu_1_letter_write), .Reset(in_1), .Memory_Update(cpu_1_write),
    .Data(input_logic_1_bus_output), .Address(cpu_1_address),
    .Screen_Row_1(screen_control_logic_1_screen_row_1),
    .Screen_Row_1_2(screen_control_logic_1_screen_row_1_2),
    .Screen_Row_2(screen_control_logic_1_screen_row_2), .Screen_Row_3(screen_control_logic_1_screen_row_3),
    .Screen_Row_4(screen_control_logic_1_screen_row_4), .Screen_Row_5(screen_control_logic_1_screen_row_5),
    .Screen_Row_6(screen_control_logic_1_screen_row_6), .Screen_Row_7(screen_control_logic_1_screen_row_7),
    .Screen_Row_8(screen_control_logic_1_screen_row_8), .Screen_Row_9(screen_control_logic_1_screen_row_9),
    .Screen_Row_A(screen_control_logic_1_screen_row_a), .Screen_Row_B(screen_control_logic_1_screen_row_b),
    .Screen_Row_C(screen_control_logic_1_screen_row_c), .Screen_Row_D(screen_control_logic_1_screen_row_d),
    .Screen_Row_E(screen_control_logic_1_screen_row_e), .Screen_Row_F(screen_control_logic_1_screen_row_f));
  DotMatrix #(.inputtype("row"), .matrixcols(16), .matrixrows(16)) dotmatrix_1 (
    .row0(screen_control_logic_1_screen_row_1), .row1(screen_control_logic_1_screen_row_1_2),
    .row2(screen_control_logic_1_screen_row_2), .row3(screen_control_logic_1_screen_row_3),
    .row4(screen_control_logic_1_screen_row_4), .row5(screen_control_logic_1_screen_row_5),
    .row6(screen_control_logic_1_screen_row_6), .row7(screen_control_logic_1_screen_row_7),
    .row8(screen_control_logic_1_screen_row_8), .row9(screen_control_logic_1_screen_row_9),
    .row10(screen_control_logic_1_screen_row_a), .row11(screen_control_logic_1_screen_row_b),
    .row12(screen_control_logic_1_screen_row_c), .row13(screen_control_logic_1_screen_row_d),
    .row14(screen_control_logic_1_screen_row_e), .row15(screen_control_logic_1_screen_row_f));
  Input_logic input_logic_1 (
    .Clock_In(clock_1_out), .Ascii_Value_in(keyboard_1_data), .Address(cpu_1_address),
    .Clock_out(input_logic_1_clock_out), .Bus_Output(input_logic_1_bus_output),
    .Ram_Rom_bus_controll_enable(input_logic_1_ram_rom_bus_controll_enable), .Enable(input_logic_1_enable));
  Clock clock_1 (.out(clock_1_out));
  ROM #(.addrWidth(15), .dataWidth(16)) rom_1 (
    .addr(memory_control_1_rom_address), .data(input_logic_1_bus_output),
    .sel(memory_control_1_enable___dissable_rom));
  RAM #(.addrWidth(15), .dataWidth(16)) ram_1 (
    .addr(memory_control_1_ram_address), .data(input_logic_1_bus_output),
    .sel(memory_control_1_enable___dissable_ram), .clk(cpu_1_write), .ld(cpu_1_read));  // open: clr
  CPU cpu_1 (
    .reset(in_2), .clock(clock_1_out), .Data(input_logic_1_bus_output), .Address(cpu_1_address),
    .Write(cpu_1_write), .Read(cpu_1_read), .Letter_write(cpu_1_letter_write), .Out(cpu_1_out),
    .Data_2(input_logic_1_bus_output), .Opcode_MIC(cpu_1_opcode_mic),
    .Micro_Instruction_OC(cpu_1_micro_instruction_oc), .PG_Address_look(cpu_1_pg_address_look),
    .internal_screen_out(cpu_1_internal_screen_out));
  // Probe on cpu_1_internal_screen_out
  Hex_Digit_Display hex_digit_display_1 (.value(cpu_1_address[15:12]));  // open: dp
  Hex_Digit_Display hex_digit_display_2 (.value(cpu_1_out[15:12]));  // open: dp
  TTY #(.trigger("falling")) tty_1 (.data(cpu_1_out[6:0]), .clk(cpu_1_letter_write), .we(1'b1), .clr(in_2));
  Hex_Digit_Display hex_digit_display_3 (.value(cpu_1_micro_instruction_oc[31:28]));  // open: dp
  Hex_Digit_Display hex_digit_display_4 (.value(cpu_1_address[11:8]));  // open: dp
  Hex_Digit_Display hex_digit_display_5 (.value(cpu_1_address[7:4]));  // open: dp
  Hex_Digit_Display hex_digit_display_6 (.value(cpu_1_out[7:4]));  // open: dp
  Hex_Digit_Display hex_digit_display_7 (.value(cpu_1_out[11:8]));  // open: dp
  Hex_Digit_Display hex_digit_display_8 (.value(cpu_1_opcode_mic[11:8]));  // open: dp
  Hex_Digit_Display hex_digit_display_9 (.value(cpu_1_opcode_mic[15:12]));  // open: dp
  Hex_Digit_Display hex_digit_display_10 (.value(cpu_1_micro_instruction_oc[23:20]));  // open: dp
  Hex_Digit_Display hex_digit_display_11 (.value(cpu_1_micro_instruction_oc[27:24]));  // open: dp
  Hex_Digit_Display hex_digit_display_12 (.value(cpu_1_address[3:0]));  // open: dp
  Hex_Digit_Display hex_digit_display_13 (.value(cpu_1_out[3:0]));  // open: dp
  Hex_Digit_Display hex_digit_display_14 (.value(cpu_1_opcode_mic[7:4]));  // open: dp
  Hex_Digit_Display hex_digit_display_15 (.value(cpu_1_opcode_mic[3:0]));  // open: dp
  Hex_Digit_Display hex_digit_display_16 (.value(cpu_1_micro_instruction_oc[15:12]));  // open: dp
  Hex_Digit_Display hex_digit_display_17 (.value(cpu_1_micro_instruction_oc[19:16]));  // open: dp
  Hex_Digit_Display hex_digit_display_18 (.value(cpu_1_pg_address_look[15:12]));  // open: dp
  Hex_Digit_Display hex_digit_display_19 (.value(cpu_1_pg_address_look[11:8]));  // open: dp
  LED _0X_Intro (.in(memory_location_panal_1__0x_intro));
  Memory_Location_panal memory_location_panal_1 (
    .Address(cpu_1_address), ._100X_Del_Old_Pixel(memory_location_panal_1__100x_del_old_pixel),
    ._200X_Calc_new_Pixel(memory_location_panal_1__200x_calc_new_pixel),
    ._300X_Write_new_Pixel(memory_location_panal_1__300x_write_new_pixel),
    ._400C_Move_Paddle_input(memory_location_panal_1__400c_move_paddle_input),
    ._500X_Paddle_collision_detection(memory_location_panal_1__500x_paddle_collision_detection),
    ._600X_Wall_Collision_Detection(memory_location_panal_1__600x_wall_collision_detection),
    .FFC0_Reading_keyboard(memory_location_panal_1_ffc0_reading_keyboard),
    .FF00_FFEF_Reading_Writting_varables(memory_location_panal_1_ff00_ffef_reading_writting_varables),
    .writting_Reading_to_screen(memory_location_panal_1_writting_reading_to_screen),
    ._0X_Intro(memory_location_panal_1__0x_intro),
    ._700X_Brick_Collision_detection(memory_location_panal_1__700x_brick_collision_detection),
    .Address_look(cpu_1_pg_address_look),
    ._2300_29FF_Game_Over(memory_location_panal_1__2300_29ff_game_over),
    ._2A00_2Aff_Win(memory_location_panal_1__2a00_2aff_win));
  LED _100X_Del_Old_Pixel (.in(memory_location_panal_1__100x_del_old_pixel));
  LED _200X_Calc_new_Pixel (.in(memory_location_panal_1__200x_calc_new_pixel));
  LED _300X_Write_new_Pixel (.in(memory_location_panal_1__300x_write_new_pixel));
  LED _400X_Move_Paddle_Input (.in(memory_location_panal_1__400c_move_paddle_input));
  LED _500X_Paddle_collision_detection (.in(memory_location_panal_1__500x_paddle_collision_detection));
  LED _600X_Wall_Collision_Detection (.in(memory_location_panal_1__600x_wall_collision_detection));
  LED _700X_Brick_Collision_Detection (.in(memory_location_panal_1__700x_brick_collision_detection));
  LED _2300_29FF_Game_Over (.in(memory_location_panal_1__2300_29ff_game_over));
  LED _2A00_2AFF_Win (.in(memory_location_panal_1__2a00_2aff_win));
  LED FFC0_Reading_keyboard (.in(memory_location_panal_1_ffc0_reading_keyboard));
  LED FF00_FFEF_Reading_Writing_variables (.in(memory_location_panal_1_ff00_ffef_reading_writting_varables));
  LED Writing_Reading_to_Screen (.in(memory_location_panal_1_writting_reading_to_screen));
  Hex_Digit_Display hex_digit_display_20 (.value(cpu_1_micro_instruction_oc[11:8]));  // open: dp
  Hex_Digit_Display hex_digit_display_21 (.value(cpu_1_micro_instruction_oc[7:4]));  // open: dp
  Hex_Digit_Display hex_digit_display_22 (.value(cpu_1_pg_address_look[3:0]));  // open: dp
  Hex_Digit_Display hex_digit_display_23 (.value(cpu_1_pg_address_look[7:4]));  // open: dp
  Hex_Digit_Display hex_digit_display_24 (.value(cpu_1_micro_instruction_oc[3:0]));  // open: dp

  // Notes on the sheet:
  //   contents of rom_1 (hex, n*v repeats v):
  //   ef00 3 8000 0 ef00 7 8001 1 a000 10 6*0 e300 8000 e200 8001 c000 e700 8002 ef00 8001 8000 ef00 8002
  //   8001 d300 8000 a000 10 479*0 a000 300
endmodule

module ALU (
  input  [15:0] A_Input,
  input  [15:0] B_Input,
  input  [2:0] ALU_State_IN,
  output [15:0] ALU_Out,
  output [3:0] ALU_State_Out
);

  wire demultiplexer_1_out1, demultiplexer_1_out2, demultiplexer_1_out3, demultiplexer_1_out4,
       demultiplexer_1_out5, demultiplexer_1_out6, demultiplexer_1_out7;
  wire [15:0] adder_1_out, and_1_out, not_1_out, or_1_out, shifter_1_out, shifter_2_out, subtractor_1_out;

  Pull_Resistor pull_resistor_1 (.node(A_Input));
  Pull_Resistor pull_resistor_2 (.node(B_Input));
  Pull_Resistor pull_resistor_3 (.node(ALU_State_IN));
  Demultiplexer #(.select(3), .disabled(0)) demultiplexer_1 (
    .out1(demultiplexer_1_out1), .out2(demultiplexer_1_out2), .out3(demultiplexer_1_out3),
    .out4(demultiplexer_1_out4), .out5(demultiplexer_1_out5), .out6(demultiplexer_1_out6),
    .out7(demultiplexer_1_out7), .in(1'b1), .sel(ALU_State_IN), .en(1'b1));  // open: out0
  Adder #(.width(16)) adder_1 (.a(A_Input), .b(B_Input), .out(adder_1_out), .cout(ALU_State_Out[0]));  // open: cin
  assign ALU_Out = demultiplexer_1_out1 ? adder_1_out : 16'bz;  // Controlled_Buffer controlled_buffer_1
  assign ALU_Out = demultiplexer_1_out2 ? subtractor_1_out : 16'bz;  // Controlled_Buffer controlled_buffer_2
  Subtractor #(.width(16)) subtractor_1 (.a(A_Input), .b(B_Input), .out(subtractor_1_out));  // open: bin, bout
  assign not_1_out = ~A_Input;  // NOT_Gate not_1, 16 bits wide
  assign ALU_Out = demultiplexer_1_out3 ? not_1_out : 16'bz;  // Controlled_Buffer controlled_buffer_3
  assign ALU_Out = demultiplexer_1_out4 ? and_1_out : 16'bz;  // Controlled_Buffer controlled_buffer_4
  assign and_1_out = A_Input & B_Input;  // AND_Gate and_1, 16 bits wide
  assign ALU_Out = demultiplexer_1_out5 ? shifter_1_out : 16'bz;  // Controlled_Buffer controlled_buffer_5
  Shifter #(.width(16), .shift("rl")) shifter_1 (.in(A_Input), .\dist (B_Input[3:0]), .out(shifter_1_out));
  assign ALU_Out = demultiplexer_1_out6 ? shifter_2_out : 16'bz;  // Controlled_Buffer controlled_buffer_6
  Shifter #(.width(16), .shift("rr")) shifter_2 (.in(A_Input), .\dist (B_Input[3:0]), .out(shifter_2_out));
  assign ALU_Out = demultiplexer_1_out7 ? or_1_out : 16'bz;  // Controlled_Buffer controlled_buffer_7
  assign or_1_out = B_Input | A_Input;  // OR_Gate or_1, 16 bits wide
  Comparator #(.width(16)) comparator_1 (
    .a(A_Input), .b(B_Input), .gt(ALU_State_Out[1]), .eq(ALU_State_Out[2]), .lt(ALU_State_Out[3]));
endmodule

// 0
module ALU_State_Out_Decoder (
  input  [3:0] State_In,
  input  reset,
  input  [2:0] State_Select,
  output [3:0] State_out
);

  wire bitselector_1_out, bitselector_2_out;
  wire [2:0] subtractor_1_out;
  wire [3:0] demultiplexer_1_out0;

  BitSelector #(.width(5)) bitselector_1 (.in({1'b0, State_In}), .out(bitselector_1_out), .sel(subtractor_1_out));
  Demultiplexer #(.select(3), .disabled(0)) demultiplexer_1 (
    .out0(demultiplexer_1_out0[0]), .out1(demultiplexer_1_out0[1]), .out2(demultiplexer_1_out0[2]),
    .out3(demultiplexer_1_out0[3]), .in(bitselector_1_out), .sel(subtractor_1_out));  // open: out4, out5, out6, out7, en
  Subtractor #(.width(3)) subtractor_1 (.a(State_Select), .b(3'b001), .out(subtractor_1_out));  // open: bin, bout
  Comparator #(.width(3)) comparator_1 (.a(State_Select), .b(3'b000));  // open: gt, eq, lt
  Clock clock_1 ();  // open: out
  BitSelector #(.width(4)) bitselector_2 (
    .in(demultiplexer_1_out0), .out(bitselector_2_out), .sel(subtractor_1_out[1:0]));
  Register_part #(.width(4)) register_1 (
    .D(demultiplexer_1_out0), .en(1'b1), .Q(State_out), .clk(bitselector_2_out), .clr(reset));
endmodule

module Internal_Screen (
  input  [15:0] \input ,
  input  Update_Values,
  output [15:0] out,
  output [3:0] _1_digit,
  output [3:0] _2_digit,
  output [3:0] _3_digit,
  output [3:0] _4_digit
);

  Register_part #(.width(16), .trigger("falling")) register_1 (
    .D(\input ), .en(1'b1), .Q({_4_digit, _3_digit, _2_digit, _1_digit}), .clk(Update_Values));  // open: clr

  assign out = {_4_digit, _3_digit, _2_digit, _1_digit};
endmodule

module Register (
  input  [15:0] in_1,
  input  Enable,
  input  reset,
  output [7:0] out_4
);

  Register_part #(.trigger("falling")) register_1 (.D(in_1[15:8]), .en(1'b1), .Q(out_4), .clk(Enable), .clr(reset));
endmodule

module _4_Bit_Register (
  input  [3:0] in_1,
  input  Enable,
  input  clock,
  input  reset,
  output [3:0] out_5
);

  Register_part #(.width(4), .trigger("falling")) register_1 (
    .D(in_1), .en(Enable), .Q(out_5), .clk(clock), .clr(reset));
endmodule

module CPU (
  input  reset,
  input  clock,
  input  [15:0] Data,
  output [15:0] Out,
  output [15:0] PG_Address_look,
  output Letter_write,
  output [15:0] Data_2,
  output [15:0] Address,
  output Write,
  output Read,
  output [15:0] Opcode_MIC,
  output [15:0] internal_screen_out,
  output [31:0] Micro_Instruction_OC
);

  wire and_1_out, or_1_out;
  wire [3:0] alu_1_alu_state_out, internal_screen_1__1_digit, internal_screen_1__2_digit,
       internal_screen_1__3_digit, internal_screen_1__4_digit;
  wire [15:0] A_Register_q, B_Register_q, controlled_buffer_1_out, Copy_Register_q, Jump_Register_q,
       X_Register_q, Y_Register_q;

  Hex_Digit_Display hex_digit_display_1 (.value(Opcode_MIC[15:12]));  // open: dp
  Hex_Digit_Display hex_digit_display_2 (.value(Opcode_MIC[11:8]));  // open: dp
  Hex_Digit_Display hex_digit_display_3 (.value(Opcode_MIC[7:4]));  // open: dp
  assign controlled_buffer_1_out = clock ? Opcode_MIC : 16'bz;  // Controlled_Buffer controlled_buffer_1
  Hex_Digit_Display hex_digit_display_4 (.value(Opcode_MIC[3:0]));  // open: dp
  Pull_Resistor pull_resistor_1 (.node({Micro_Instruction_OC[31:26], Letter_write, Micro_Instruction_OC[24:0]}));
  Register register_1 (.in_1(Out), .Enable(Micro_Instruction_OC[24]), .out_4(Opcode_MIC[11:4]), .reset(reset));
  ROM #(.addrWidth(16), .dataWidth(32)) rom_1 (
    .addr(controlled_buffer_1_out),
    .data({Micro_Instruction_OC[31:26], Letter_write, Micro_Instruction_OC[24:0]}), .sel(clock));
  Hex_Digit_Display hex_digit_display_5 (.value(Micro_Instruction_OC[31:28]));  // open: dp
  Counter #(.width(4), .max('hf), .trigger("falling")) counter_1 (
    .count(1'b1), .Q(Opcode_MIC[3:0]), .clk(clock), .clr(or_1_out));  // open: load, D, carry
  or or_1 (or_1_out, reset, Micro_Instruction_OC[23]);
  ALU_State_Out_Decoder alu_state_out_decoder_1 (
    .State_In(alu_1_alu_state_out), .State_Select(Micro_Instruction_OC[22:20]),
    .State_out(Opcode_MIC[15:12]), .reset(or_1_out));
  Hex_Digit_Display hex_digit_display_6 (.value({Micro_Instruction_OC[27:26], Letter_write, Micro_Instruction_OC[24]}));  // open: dp
  Hex_Digit_Display hex_digit_display_7 (.value(Micro_Instruction_OC[23:20]));  // open: dp
  Register_part #(.width(16), .trigger("falling")) register_2 (
    .D(Out), .Q(Address), .clk(Micro_Instruction_OC[16]), .clr(reset));  // open: en
  Hex_Digit_Display hex_digit_display_8 (.value(internal_screen_1__4_digit));  // open: dp
  Hex_Digit_Display hex_digit_display_9 (.value(Micro_Instruction_OC[19:16]));  // open: dp
  Hex_Digit_Display hex_digit_display_10 (.value(Micro_Instruction_OC[15:12]));  // open: dp
  Hex_Digit_Display hex_digit_display_11 (.value(internal_screen_1__3_digit));  // open: dp
  Hex_Digit_Display hex_digit_display_12 (.value(internal_screen_1__2_digit));  // open: dp
  Hex_Digit_Display hex_digit_display_13 (.value(Micro_Instruction_OC[11:8]));  // open: dp
  Hex_Digit_Display hex_digit_display_14 (.value(Micro_Instruction_OC[7:4]));  // open: dp
  Hex_Digit_Display hex_digit_display_15 (.value(Out[15:12]));  // open: dp
  and and_1 (and_1_out, clock, Micro_Instruction_OC[15]);
  not not_1 (Write, and_1_out);
  Hex_Digit_Display hex_digit_display_16 (.value(internal_screen_1__1_digit));  // open: dp
  Internal_Screen internal_screen_1 (
    .\input (Out), ._1_digit(internal_screen_1__1_digit), ._2_digit(internal_screen_1__2_digit),
    .Update_Values(Micro_Instruction_OC[13]), ._3_digit(internal_screen_1__3_digit),
    ._4_digit(internal_screen_1__4_digit), .out(internal_screen_out));
  Hex_Digit_Display hex_digit_display_17 (.value(Micro_Instruction_OC[3:0]));  // open: dp
  Hex_Digit_Display hex_digit_display_18 (.value(Out[11:8]));  // open: dp
  Hex_Digit_Display hex_digit_display_19 (.value(Out[7:4]));  // open: dp
  Counter #(.width(16), .max('hffff), .trigger("falling")) counter_2 (
    .load(Micro_Instruction_OC[19]), .D(Out), .count(Micro_Instruction_OC[18]), .Q(PG_Address_look),
    .clk(clock), .clr(reset));  // open: carry
  Hex_Digit_Display hex_digit_display_20 (.value(Out[3:0]));  // open: dp
  Pull_Resistor pull_resistor_2 (.node(Out));
  assign Out = Micro_Instruction_OC[17] ? PG_Address_look : 16'bz;  // Controlled_Buffer controlled_buffer_2
  assign Data_2 = Micro_Instruction_OC[15] ? Out : 16'bz;  // Controlled_Buffer controlled_buffer_3
  assign Out = Micro_Instruction_OC[14] ? Data : 16'bz;  // Controlled_Buffer controlled_buffer_4
  assign Out = Micro_Instruction_OC[26] ? Copy_Register_q : 16'bz;  // Controlled_Buffer controlled_buffer_5
  Register_part #(.width(16), .trigger("falling")) Copy_Register (
    .D(Out), .Q(Copy_Register_q), .clk(Micro_Instruction_OC[27]));  // open: en, clr
  Register_part #(.width(16), .trigger("falling")) X_Register (
    .D(Out), .en(1'b1), .Q(X_Register_q), .clk(Micro_Instruction_OC[3]));  // open: clr
  assign Out = Micro_Instruction_OC[4] ? X_Register_q : 16'bz;  // Controlled_Buffer controlled_buffer_6
  Register_part #(.width(16), .trigger("falling")) Y_Register (
    .D(Out), .en(1'b1), .Q(Y_Register_q), .clk(Micro_Instruction_OC[5]));  // open: clr
  assign Out = Micro_Instruction_OC[6] ? Y_Register_q : 16'bz;  // Controlled_Buffer controlled_buffer_7
  Register_part #(.width(16), .trigger("falling")) A_Register (
    .D(Out), .en(1'b1), .Q(A_Register_q), .clk(Micro_Instruction_OC[7]));  // open: clr
  assign Out = Micro_Instruction_OC[8] ? A_Register_q : 16'bz;  // Controlled_Buffer controlled_buffer_8
  ALU alu_1 (
    .A_Input(A_Register_q), .B_Input(B_Register_q), .ALU_State_IN(Micro_Instruction_OC[2:0]), .ALU_Out(Out),
    .ALU_State_Out(alu_1_alu_state_out));
  Register_part #(.width(16), .trigger("falling")) B_Register (
    .D(Out), .en(1'b1), .Q(B_Register_q), .clk(Micro_Instruction_OC[9]));  // open: clr
  assign Out = Micro_Instruction_OC[10] ? B_Register_q : 16'bz;  // Controlled_Buffer controlled_buffer_9
  Register_part #(.width(16), .trigger("falling")) Jump_Register (
    .D(Out), .en(1'b1), .Q(Jump_Register_q), .clk(Micro_Instruction_OC[11]));  // open: clr
  assign Out = Micro_Instruction_OC[12] ? Jump_Register_q : 16'bz;  // Controlled_Buffer controlled_buffer_10

  assign Micro_Instruction_OC[25] = Letter_write;
  assign Read = Micro_Instruction_OC[14];

  // Notes on the sheet:
  //   contents of rom_1 (hex, n*v repeats v):
  //   30000 1044000 800000 13*0 30000 1044000 30000 14000 44020 800000 10*0 30000 1044000 30000 14000
  //   44200 800000 10*0 30000 1044000 30000 14000 44080 800000 10*0 30000 1044000 30000 14000 48010 800000
  //   10*0 30000 1044000 30000 14000 48040 800000 10*0 30000 1044000 30000 14000 48400 800000 10*0 30000
  //   1044000 30000 14000 48100 800000 2442*0 30000 1044000 30000 84000 800000 11*0 30000 1044000 30000
  //   84000 800000 11*0 30000 1044000 340000 800000 28*0 30000 1044000 240000 800000 12*0 30000 1044000
  //   80100 800000 172*0 30000 1044000 30000 60800 84000 800000 58*0 30000 1044000 81000 800000 188*0
  //   30000 1044000 81 800000 12*0 30000 1044000 82 800000 12*0 30000 1044000 83 800000 12*0 30000 1044000
  //   84 800000 12*0 30000 1044000 85 800000 12*0 30000 1044000 86 800000 12*0 30000 1044000 87 800000
  //   156*0 30000 1044000 2100 800000 12*0 30000 1044000 2010 800000 12*0 30000 1044000 2040 800000 12*0
  //   30000 1044000 30000 54000 6000 800000 202*0 30000 1044000 30000 14000 44008 800000 10*0 30000
  //   1044000 30000 14000 44020 800000 10*0 30000 1044000 30000 14000 44200 800000 10*0 30000 1044000
  //   30000 14000 44080 800000 10*0 30000 1044000 30000 14000 48010 800000 10*0 30000 1044000 30000 14000
  //   48040 800000 10*0 30000 1044000 30000 14000 48400 800000 10*0 30000 1044000 30000 14000 48100 800000
  //   10*0 30000 1044000 2004000 800000 12*0 30000 1044000 30000 14000 14000 44008 800000 9*0 30000
  //   1044000 30000 14000 14000 44020 800000 9*0 30000 1044000 30000 14000 14000 44200 800000 9*0 30000
  //   1044000 30000 14000 14000 48010 800000 9*0 30000 1044000 30000 14000 14000 48400 800000 9*0 30000
  //   1044000 30000 14000 14000 48100 800000 9*0 30000 1044000 30000 54000 8004000 30000 54000 4008000
  //   800000 6983*0 30000 1044000 230000 284000 a00000 8157*0 330000 384000 b00000
endmodule

module Screen_Control_logic (
  input  Screen_Update,
  input  Reset,
  input  Memory_Update,
  input  [15:0] Data,
  input  [15:0] Address,
  output [15:0] Screen_Row_1,
  output [15:0] Screen_Row_1_2,
  output [15:0] Screen_Row_2,
  output [15:0] Screen_Row_3,
  output [15:0] Screen_Row_4,
  output [15:0] Screen_Row_5,
  output [15:0] Screen_Row_6,
  output [15:0] Screen_Row_7,
  output [15:0] Screen_Row_8,
  output [15:0] Screen_Row_9,
  output [15:0] Screen_Row_A,
  output [15:0] Screen_Row_B,
  output [15:0] Screen_Row_C,
  output [15:0] Screen_Row_D,
  output [15:0] Screen_Row_E,
  output [15:0] Screen_Row_F
);

  wire comparator_1_eq, comparator_2_eq, comparator_3_eq, comparator_4_eq, comparator_5_eq, comparator_6_eq,
       comparator_7_eq, comparator_8_eq, comparator_9_eq, comparator_10_eq, comparator_11_eq,
       comparator_12_eq, comparator_13_eq, comparator_14_eq, comparator_15_eq, comparator_16_eq;
  wire [15:0] register_1_q, register_4_q, register_5_q, register_7_q, register_10_q, register_12_q,
       register_13_q, register_15_q, register_18_q, register_19_q, register_21_q, register_24_q,
       register_26_q, register_28_q, register_30_q, register_32_q;

  Comparator #(.width(16), .mode("unsigned")) comparator_1 (
    .a(16'hfff0), .b(Address), .eq(comparator_1_eq));  // open: gt, lt
  Comparator #(.width(16), .mode("unsigned")) comparator_2 (
    .a(16'hfff1), .b(Address), .eq(comparator_2_eq));  // open: gt, lt
  Comparator #(.width(16), .mode("unsigned")) comparator_3 (
    .a(16'hfff2), .b(Address), .eq(comparator_3_eq));  // open: gt, lt
  Comparator #(.width(16), .mode("unsigned")) comparator_4 (
    .a(16'hfff3), .b(Address), .eq(comparator_4_eq));  // open: gt, lt
  Comparator #(.width(16), .mode("unsigned")) comparator_5 (
    .a(16'hfff4), .b(Address), .eq(comparator_5_eq));  // open: gt, lt
  Comparator #(.width(16), .mode("unsigned")) comparator_6 (
    .a(16'hfff5), .b(Address), .eq(comparator_6_eq));  // open: gt, lt
  Comparator #(.width(16), .mode("unsigned")) comparator_7 (
    .a(16'hfff6), .b(Address), .eq(comparator_7_eq));  // open: gt, lt
  Comparator #(.width(16), .mode("unsigned")) comparator_8 (
    .a(16'hfff7), .b(Address), .eq(comparator_8_eq));  // open: gt, lt
  Comparator #(.width(16), .mode("unsigned")) comparator_9 (
    .a(16'hfff8), .b(Address), .eq(comparator_9_eq));  // open: gt, lt
  Comparator #(.width(16), .mode("unsigned")) comparator_10 (
    .a(16'hfff9), .b(Address), .eq(comparator_10_eq));  // open: gt, lt
  Comparator #(.width(16), .mode("unsigned")) comparator_11 (
    .a(16'hfffa), .b(Address), .eq(comparator_11_eq));  // open: gt, lt
  Comparator #(.width(16), .mode("unsigned")) comparator_12 (
    .a(16'hfffb), .b(Address), .eq(comparator_12_eq));  // open: gt, lt
  Comparator #(.width(16), .mode("unsigned")) comparator_13 (
    .a(16'hfffc), .b(Address), .eq(comparator_13_eq));  // open: gt, lt
  Comparator #(.width(16), .mode("unsigned")) comparator_14 (
    .a(16'hfffd), .b(Address), .eq(comparator_14_eq));  // open: gt, lt
  Comparator #(.width(16), .mode("unsigned")) comparator_15 (
    .a(16'hfffe), .b(Address), .eq(comparator_15_eq));  // open: gt, lt
  Comparator #(.width(16), .mode("unsigned")) comparator_16 (
    .a({16{1'b1}}), .b(Address), .eq(comparator_16_eq));  // open: gt, lt
  Register_part #(.width(16), .trigger("falling")) register_1 (
    .D(Data), .en(comparator_1_eq), .Q(register_1_q), .clk(Memory_Update), .clr(Reset));
  Register_part #(.width(16)) register_2 (
    .D(register_1_q), .en(Screen_Update), .Q(Screen_Row_1), .clk(Screen_Update), .clr(Reset));
  Register_part #(.width(16)) register_3 (
    .D(register_4_q), .en(Screen_Update), .Q(Screen_Row_1_2), .clk(Screen_Update), .clr(Reset));
  Register_part #(.width(16), .trigger("falling")) register_4 (
    .D(Data), .en(comparator_2_eq), .Q(register_4_q), .clk(Memory_Update), .clr(Reset));
  Register_part #(.width(16), .trigger("falling")) register_5 (
    .D(Data), .en(comparator_3_eq), .Q(register_5_q), .clk(Memory_Update), .clr(Reset));
  Register_part #(.width(16)) register_6 (
    .D(register_5_q), .en(Screen_Update), .Q(Screen_Row_2), .clk(Screen_Update), .clr(Reset));
  Register_part #(.width(16), .trigger("falling")) register_7 (
    .D(Data), .en(comparator_4_eq), .Q(register_7_q), .clk(Memory_Update), .clr(Reset));
  Register_part #(.width(16)) register_8 (
    .D(register_7_q), .en(Screen_Update), .Q(Screen_Row_3), .clk(Screen_Update), .clr(Reset));
  Register_part #(.width(16)) register_9 (
    .D(register_10_q), .en(Screen_Update), .Q(Screen_Row_4), .clk(Screen_Update), .clr(Reset));
  Register_part #(.width(16), .trigger("falling")) register_10 (
    .D(Data), .en(comparator_5_eq), .Q(register_10_q), .clk(Memory_Update), .clr(Reset));
  Register_part #(.width(16)) register_11 (
    .D(register_12_q), .en(Screen_Update), .Q(Screen_Row_5), .clk(Screen_Update), .clr(Reset));
  Register_part #(.width(16), .trigger("falling")) register_12 (
    .D(Data), .en(comparator_6_eq), .Q(register_12_q), .clk(Memory_Update), .clr(Reset));
  Register_part #(.width(16), .trigger("falling")) register_13 (
    .D(Data), .en(comparator_7_eq), .Q(register_13_q), .clk(Memory_Update), .clr(Reset));
  Register_part #(.width(16)) register_14 (
    .D(register_13_q), .en(Screen_Update), .Q(Screen_Row_6), .clk(Screen_Update), .clr(Reset));
  Register_part #(.width(16), .trigger("falling")) register_15 (
    .D(Data), .en(comparator_8_eq), .Q(register_15_q), .clk(Memory_Update), .clr(Reset));
  Register_part #(.width(16)) register_16 (
    .D(register_15_q), .en(Screen_Update), .Q(Screen_Row_7), .clk(Screen_Update), .clr(Reset));
  Register_part #(.width(16)) register_17 (
    .D(register_18_q), .en(Screen_Update), .Q(Screen_Row_8), .clk(Screen_Update), .clr(Reset));
  Register_part #(.width(16), .trigger("falling")) register_18 (
    .D(Data), .en(comparator_9_eq), .Q(register_18_q), .clk(Memory_Update), .clr(Reset));
  Register_part #(.width(16), .trigger("falling")) register_19 (
    .D(Data), .en(comparator_10_eq), .Q(register_19_q), .clk(Memory_Update), .clr(Reset));
  Register_part #(.width(16)) register_20 (
    .D(register_19_q), .en(Screen_Update), .Q(Screen_Row_9), .clk(Screen_Update), .clr(Reset));
  Register_part #(.width(16), .trigger("falling")) register_21 (
    .D(Data), .en(comparator_11_eq), .Q(register_21_q), .clk(Memory_Update), .clr(Reset));
  Register_part #(.width(16)) register_22 (
    .D(register_21_q), .en(Screen_Update), .Q(Screen_Row_A), .clk(Screen_Update), .clr(Reset));
  Register_part #(.width(16)) register_23 (
    .D(register_24_q), .en(Screen_Update), .Q(Screen_Row_B), .clk(Screen_Update), .clr(Reset));
  Register_part #(.width(16), .trigger("falling")) register_24 (
    .D(Data), .en(comparator_12_eq), .Q(register_24_q), .clk(Memory_Update), .clr(Reset));
  Register_part #(.width(16)) register_25 (
    .D(register_26_q), .en(Screen_Update), .Q(Screen_Row_C), .clk(Screen_Update), .clr(Reset));
  Register_part #(.width(16), .trigger("falling")) register_26 (
    .D(Data), .en(comparator_13_eq), .Q(register_26_q), .clk(Memory_Update), .clr(Reset));
  Register_part #(.width(16)) register_27 (
    .D(register_28_q), .en(Screen_Update), .Q(Screen_Row_D), .clk(Screen_Update), .clr(Reset));
  Register_part #(.width(16), .trigger("falling")) register_28 (
    .D(Data), .en(comparator_14_eq), .Q(register_28_q), .clk(Memory_Update), .clr(Reset));
  Register_part #(.width(16)) register_29 (
    .D(register_30_q), .en(Screen_Update), .Q(Screen_Row_E), .clk(Screen_Update), .clr(Reset));
  Register_part #(.width(16), .trigger("falling")) register_30 (
    .D(Data), .en(comparator_15_eq), .Q(register_30_q), .clk(Memory_Update), .clr(Reset));
  Register_part #(.width(16)) register_31 (
    .D(register_32_q), .en(Screen_Update), .Q(Screen_Row_F), .clk(Screen_Update), .clr(Reset));
  Register_part #(.width(16), .trigger("falling")) register_32 (
    .D(Data), .en(comparator_16_eq), .Q(register_32_q), .clk(Memory_Update), .clr(Reset));
endmodule

module Input_logic (
  input  Clock_In,
  input  [6:0] Ascii_Value_in,
  input  [15:0] Address,
  output Clock_out,
  output Enable,
  output [15:0] Bus_Output,
  output Ram_Rom_bus_controll_enable
);

  wire [6:0] register_1_q;

  T_Flip_Flop t_ff_1 (.clk(Clock_In), .T(Clock_In), .Qn(Clock_out));  // open: Q, preset, reset, en
  Comparator #(.width(16)) comparator_1 (.a(Address), .b(16'hffc0), .eq(Enable));  // open: gt, lt
  not not_1 (Ram_Rom_bus_controll_enable, Enable);
  Register_part #(.width(7)) register_1 (.D(Ascii_Value_in), .en(1'b1), .Q(register_1_q), .clk(Enable));  // open: clr
  assign Bus_Output[6:0] = Enable ? register_1_q : 7'bz;  // Controlled_Buffer controlled_buffer_1
endmodule

module Memory_Location_panal (
  input  [15:0] Address_look,
  input  [15:0] Address,
  output _0X_Intro,
  output _100X_Del_Old_Pixel,
  output _200X_Calc_new_Pixel,
  output _300X_Write_new_Pixel,
  output _400C_Move_Paddle_input,
  output _500X_Paddle_collision_detection,
  output _600X_Wall_Collision_Detection,
  output _700X_Brick_Collision_detection,
  output _2300_29FF_Game_Over,
  output _2A00_2Aff_Win,
  output FFC0_Reading_keyboard,
  output FF00_FFEF_Reading_Writting_varables,
  output writting_Reading_to_screen
);

  Between between_1 (.Top_between({16{1'b0}}), .Address(Address_look), .bottom_between(16'hff), .out_4(_0X_Intro));
  Between between_2 (
    .Top_between(16'h100), .Address(Address_look), .bottom_between(16'h1ff), .out_4(_100X_Del_Old_Pixel));
  Between between_3 (
    .Top_between(16'h200), .Address(Address_look), .bottom_between(16'h2ff), .out_4(_200X_Calc_new_Pixel));
  Between between_4 (
    .Top_between(16'h300), .Address(Address_look), .bottom_between(16'h3ff), .out_4(_300X_Write_new_Pixel));
  Between between_5 (
    .Top_between(16'h400), .Address(Address_look), .bottom_between(16'h4ff), .out_4(_400C_Move_Paddle_input));
  Between between_6 (
    .Top_between(16'h500), .Address(Address_look), .bottom_between(16'h5ff),
    .out_4(_500X_Paddle_collision_detection));
  Between between_7 (
    .Top_between(16'h600), .Address(Address_look), .bottom_between(16'h6ff),
    .out_4(_600X_Wall_Collision_Detection));
  Between between_8 (
    .Top_between(16'h700), .Address(Address_look), .bottom_between(16'h7ff),
    .out_4(_700X_Brick_Collision_detection));
  Between between_9 (
    .Top_between(16'h2300), .Address(Address_look), .bottom_between(16'h23ff), .out_4(_2300_29FF_Game_Over));
  Between between_10 (
    .Top_between(16'h2a00), .Address(Address_look), .bottom_between(16'h2aff), .out_4(_2A00_2Aff_Win));
  Between between_11 (
    .Top_between(16'hffc0), .Address(Address), .bottom_between(16'hffc0), .out_4(FFC0_Reading_keyboard));
  Between between_12 (
    .Top_between(16'hff00), .Address(Address), .bottom_between(16'hffef),
    .out_4(FF00_FFEF_Reading_Writting_varables));
  Between between_13 (
    .Top_between(16'hfff0), .Address(Address), .bottom_between({16{1'b1}}), .out_4(writting_Reading_to_screen));
  LED u__0X_Intro (.in(_0X_Intro));
  LED u__100X_Del_Old_Pixel (.in(_100X_Del_Old_Pixel));
  LED u__200X_Calc_new_Pixel (.in(_200X_Calc_new_Pixel));
  LED u__300X_Write_new_Pixel (.in(_300X_Write_new_Pixel));
  LED _400X_Move_Paddle_Input (.in(_400C_Move_Paddle_input));
  LED u__500X_Paddle_collision_detection (.in(_500X_Paddle_collision_detection));
  LED u__600X_Wall_Collision_Detection (.in(_600X_Wall_Collision_Detection));
  LED u__700X_Brick_Collision_detection (.in(_700X_Brick_Collision_detection));
  LED u__2300_29FF_Game_Over (.in(_2300_29FF_Game_Over));
  LED u__2A00_2Aff_Win (.in(_2A00_2Aff_Win));
  LED u_FFC0_Reading_keyboard (.in(FFC0_Reading_keyboard));
  LED FF00_FFEF_Reading_Writing_variables (.in(FF00_FFEF_Reading_Writting_varables));
  LED Writing_Reading_to_Screen (.in(writting_Reading_to_screen));
endmodule

module Between (
  input  [15:0] Top_between,
  input  [15:0] Address,
  input  [15:0] bottom_between,
  output out_4
);

  wire comparator_1_eq, comparator_1_lt, comparator_2_eq, comparator_2_lt, or_1_out, or_2_out;

  Comparator #(.width(16), .mode("unsigned")) comparator_1 (
    .a(Top_between), .b(Address), .eq(comparator_1_eq), .lt(comparator_1_lt));  // open: gt
  or or_1 (or_1_out, comparator_1_eq, comparator_1_lt);
  Comparator #(.width(16), .mode("unsigned")) comparator_2 (
    .a(Address), .b(bottom_between), .eq(comparator_2_eq), .lt(comparator_2_lt));  // open: gt
  or or_2 (or_2_out, comparator_2_eq, comparator_2_lt);
  and and_1 (out_4, or_1_out, or_2_out);
endmodule

module Memory_control (
  input  Read,
  input  [15:0] Address,
  input  enable___dissable_memory,
  output [14:0] ROM_address,
  output enable___dissable_ROM,
  output enable___dissable_RAM,
  output [14:0] RAM_address
);

  and and_1 (enable___dissable_ROM, ~Address[15], Read, enable___dissable_memory);  // AND_Gate
  and and_2 (enable___dissable_RAM, Address[15], enable___dissable_memory);

  assign RAM_address = Address[14:0];
  assign ROM_address = Address[14:0];
endmodule
